// Logisim project BancoRegistros.circ as structural Verilog: 1 circuit, main circuit BancoRegistros
module BancoRegistros (
  input  CLR,
  input  [31:0] di,
  input  [4:0] a1,
  input  CLK,
  input  we,
  input  [4:0] a2,
  input  [4:0] ad,
  output [31:0] do1,
  output [31:0] do2
);

  wire demultiplexer_1_out1, demultiplexer_1_out2, demultiplexer_1_out3, demultiplexer_1_out4,
       demultiplexer_1_out5, demultiplexer_1_out6, demultiplexer_1_out7;
  wire [31:0] R0_q, R1_q, R2_q, R3_q, R4_q, R5_q, R6_q, R7_q;

  Demultiplexer #(.select(5)) demultiplexer_1 (
    .out1(demultiplexer_1_out1), .out2(demultiplexer_1_out2), .out3(demultiplexer_1_out3),
    .out4(demultiplexer_1_out4), .out5(demultiplexer_1_out5), .out6(demultiplexer_1_out6),
    .out7(demultiplexer_1_out7), .in(CLK), .sel(ad), .en(we));  // open: out0, out8, out9, out10, out11, out12, out13, out14, out15, out16, out17, out18, out19, out20, out21, out22, out23, out24, out25, out26, out27, out28, out29, out30, out31
  Register #(.width(32)) R0 (.Q(R0_q));  // open: D, en, clk, clr
  Register #(.width(32)) R1 (.D(di), .Q(R1_q), .clk(demultiplexer_1_out1), .clr(CLR));  // open: en
  Register #(.width(32)) R2 (.D(di), .Q(R2_q), .clk(demultiplexer_1_out2), .clr(CLR));  // open: en
  Register #(.width(32)) R3 (.D(di), .Q(R3_q), .clk(demultiplexer_1_out3), .clr(CLR));  // open: en
  Register #(.width(32)) R4 (.D(di), .Q(R4_q), .clk(demultiplexer_1_out4), .clr(CLR));  // open: en
  Register #(.width(32)) R5 (.D(di), .Q(R5_q), .clk(demultiplexer_1_out5), .clr(CLR));  // open: en
  Register #(.width(32)) R6 (.D(di), .Q(R6_q), .clk(demultiplexer_1_out6), .clr(CLR));  // open: en
  Register #(.width(32)) R7 (.D(di), .Q(R7_q), .clk(demultiplexer_1_out7), .clr(CLR));  // open: en
  Multiplexer #(.select(5), .width(32)) multiplexer_1 (
    .in0(R0_q), .in1(R1_q), .in2(R2_q), .in3(R3_q), .in4(R4_q), .in5(R5_q), .in6(R6_q), .in7(R7_q),
    .out(do1), .sel(a1));  // open: in8, in9, in10, in11, in12, in13, in14, in15, in16, in17, in18, in19, in20, in21, in22, in23, in24, in25, in26, in27, in28, in29, in30, in31, en
  Multiplexer #(.select(5), .width(32)) multiplexer_2 (
    .in0(R0_q), .in1(R1_q), .in2(R2_q), .in3(R3_q), .in4(R4_q), .in5(R5_q), .in6(R6_q), .in7(R7_q),
    .out(do2), .sel(a2));  // open: in8, in9, in10, in11, in12, in13, in14, in15, in16, in17, in18, in19, in20, in21, in22, in23, in24, in25, in26, in27, in28, in29, in30, in31, en

  // Notes on the sheet:
  //   Designed by: Eng. Oscar Hurtado (TxOs) 
  //   Under License Creative Commons CC BY-SA
  //   https://creativecommons.org/share-your-work/cclicenses/
  //   Nota: El registro cero R0 siempre retorna el valor de 'cero'
  //   BANCO DE REGISTROS
endmodule
