// Logisim project alu.circ as structural Verilog: 1 circuit, main circuit alu
// ALU
module alu (
  input  [31:0] in_1,
  input  [31:0] in_2,
  input  [3:0] in_3,
  output [31:0] out_4
);

  wire [31:0] adder_1_out, and_out, or_1_out, subtractor_1_out;

  Adder #(.width(32)) adder_1 (.a(in_1), .b(in_2), .out(adder_1_out));  // open: cin, cout
  Subtractor #(.width(32)) subtractor_1 (.a(in_1), .b(in_2), .out(subtractor_1_out));  // open: bin, bout
  assign and_out = in_2 & in_1;  // AND_Gate and, 32 bits wide
  assign or_1_out = in_2 | in_1;  // OR_Gate or_1, 32 bits wide
  Multiplexer #(.select(4), .width(32)) multiplexer_1 (
    .in0(adder_1_out), .in1(subtractor_1_out), .in12(or_1_out), .in14(and_out), .out(out_4), .sel(in_3));  // open: in2, in3, in4, in5, in6, in7, in8, in9, in10, in11, in13, in15, en

  // Notes on the sheet:
  //   ALU
  //   Designed by: Eng. Oscar Hurtado (TxOs) 
  //   Under License Creative Commons CC BY-SA
  //   https://creativecommons.org/share-your-work/cclicenses/
endmodule
