// Logisim project unidadDeControl.circ as structural Verilog: 2 circuits, main circuit salidas
// S
module salidas (
  input  [4:0] Din,
  input  EN,
  output [4:0] Dout
);

  assign Dout[0] = EN ? Din[0] : 1'bz;  // Controlled_Buffer controlled_buffer_1
  assign Dout[1] = EN ? Din[1] : 1'bz;  // Controlled_Buffer controlled_buffer_2
  assign Dout[2] = EN ? Din[2] : 1'bz;  // Controlled_Buffer controlled_buffer_3
  assign Dout[3] = EN ? Din[3] : 1'bz;  // Controlled_Buffer controlled_buffer_4
  assign Dout[4] = EN ? Din[4] : 1'bz;  // Controlled_Buffer controlled_buffer_5

  // Notes on the sheet:
  //   Módulo Salidas
  //   Designed by: Eng. Oscar Hurtado (TxOs) 
  //   Under License Creative Commons CC BY-SA
  //   https://creativecommons.org/share-your-work/cclicenses/
endmodule

// Unidad de Control
module unidadDeControl (
  input  [6:0] F7,
  input  [2:0] F3,
  input  [6:0] opcode,
  output we,
  output alu1,
  output alu2,
  output alu3,
  output alu4
);

  wire and_1_out, and_2_out, and_3_out, comparator_3_eq, comparator_4_eq;
  wire [1:0] comparator_1_eq;

  Comparator #(.width(3)) comparator_1 (.a(F3), .b(3'b000), .eq(comparator_1_eq[0]));  // open: gt, lt
  Comparator #(.width(3)) comparator_2 (.a(F3), .b(3'b111), .eq(comparator_1_eq[1]));  // open: gt, lt
  Comparator #(.width(7)) comparator_3 (.a(opcode), .b(7'b0110011), .eq(comparator_3_eq));  // open: gt, lt
  Comparator #(.width(7)) comparator_4 (.a(F7), .b(7'b0100000), .eq(comparator_4_eq));  // open: gt, lt
  and and_1 (and_1_out, ~comparator_4_eq, comparator_1_eq[0], comparator_3_eq);  // AND_Gate
  and and_2 (and_2_out, comparator_4_eq, comparator_1_eq[0], comparator_3_eq);
  and and_3 (and_3_out, ~comparator_4_eq, comparator_1_eq[1], comparator_3_eq);  // AND_Gate
  salidas salidas_1 (.Din(5'b00001), .EN(and_1_out), .Dout({alu4, alu3, alu2, alu1, we}));
  salidas salidas_2 (.Din(5'b00011), .EN(and_2_out), .Dout({alu4, alu3, alu2, alu1, we}));
  salidas salidas_3 (.Din(5'b11101), .EN(and_3_out), .Dout({alu4, alu3, alu2, alu1, we}));

  // Notes on the sheet:
  //   Banco De Registros
  //   Designed by: Eng. Oscar Hurtado (TxOs) 
  //   Under License Creative Commons CC BY-SA
  //   https://creativecommons.org/share-your-work/cclicenses/
  //   R 0110011
  //   0100000
  //   000
  //   add/sub
  //   111
  //   and
  //   FUNC 3
  //   OPCODE
  //   FUNCTION 7
  //   F3
  //   opcode
  //   F7
  //   R ADD
  //   R SUB
  //   R AND
  //   control signals
  //   alu4 We
  //   0000 1
  //   0001 1
  //   11101
endmodule
